# Fritzing sketch Po_PWM_Ctrl_Buzzer (saved by Fritzing 0.9.0b)
breadboards: 1

parts:
  Part1 = Arduino Uno (Rev3)
  R1 = Trimmer Potentiometer [maximum_resistance=10kΩ package=THT]
  J1 = Piezo Speaker

nets:
  N1: Part1.A1, R1.wiper
  N2: Part1.GND, R1.leg2, J1.pin1
  N3: Part1.D3_PWM, J1.pin2
  N4: Part1.5V, R1.leg1
